# Fritzing sketch fritzing schematic (saved by Fritzing 0.9.3b)
breadboards: 2

parts:
  Part1 = Arduino Uno (Rev3) - ICSP
  U1 = NodeMCU V3.0
  Part2 = Logic Level Converter
  R1 = PHOTOCELL [package=photocell]
  R2 = Resistor [tolerance=±5% resistance=5.1k package=THT]
  LED1 = LED - 3mm [color="Green (555nm)" package="3 mm [THT]"]
  R3 = Resistor [tolerance=±20% resistance=1k package=THT]
  Part3 = MQ-3 breakout
  DHT1 = DHT11 Humitidy and Temperature Sensor
  R4 = Resistor [tolerance=±5% resistance=4.7k package=THT]
  R5 = Resistor [tolerance=±5% resistance=330 package=THT]
  U3 = POT [package=pot_alpha_rv16af-20]
  S1 = Pushbutton [package="[SMD]"]
  S2 = Pushbutton [package="[SMD]"]
  S3 = Pushbutton [package="[SMD]"]
  R6 = Resistor [tolerance=±5% resistance=10k package=THT]
  R7 = Resistor [tolerance=±5% resistance=10k package=THT]
  R8 = Resistor [tolerance=±5% resistance=10k package=THT]
  U2 = LCD-16X2 [package=lcd-16x2]
  LED2 = LED - 3mm [color="Green (555nm)" package="3 mm [THT]"]
  LED3 = LED - 3mm [color="Red (633nm)" package="3 mm [THT]"]
  R9 = Resistor [tolerance=±5% resistance=1k package=THT]
  R10 = Resistor [tolerance=±5% resistance=330 package=THT]
  LED4 = LED - 3mm [color="Yellow (592nm)" package="3 mm [THT]"]
  R11 = Resistor [tolerance=±5% resistance=330 package=THT]
  S4 = Pushbutton [package="[SMD]"]
  R12 = Resistor [tolerance=±5% resistance=10k package=THT]

nets:
  N1: Part1.A0, R1.P$2, R2.Pin_0
  N2: Part1.A1, Part3.AO
  N3: Part1.A2, R10.Pin_0
  N4: Part1.A3, R9.Pin_0
  N5: Part1.A4/SDA, Part2.TX_HV
  N6: Part1.A5/SCL, Part2.RX_HV
  N7: Part1.ICSP_MISO, Part1.D12/MISO, U2.DB7
  N8: Part1.ICSP_MOSI, Part1.D11_PWM/MOSI, U2.DB6
  VDD: Part1.5V, Part2.HV, R1.P$1, Part3.VCC, DHT1.VDD, R4.Pin_1, R6.Pin_1, R7.Pin_1, R8.Pin_1, U2.VDD
  N9: Part1.D8, U2.E
  N10: Part1.D9_PWM, U2.DB4
  N11: Part1.D10_PWM/SS, U2.DB5
  N12: Part1.D2, DHT1.DATA, R4.Pin_0
  N13: Part1.D3_PWM, S1.Pin_3, S1.Pin_4, R6.Pin_0
  N14: Part1.D4, S2.Pin_3, S2.Pin_4, R7.Pin_0
  N15: Part1.D5_PWM, S3.Pin_3, S3.Pin_4, R8.Pin_0
  N16: Part1.D6_PWM, R5.Pin_0
  N17: Part1.D7, U2.RS
  GND: Part1.GND, U1.GND, Part2.GND, R2.Pin_1, LED1.cathode, Part3.GND, DHT1.GND, U3.E, S1.Pin_1, S1.Pin_2, S2.Pin_1, S2.Pin_2, S3.Pin_1, S3.Pin_2, U2.VSS, U2.R_W, U2.K, LED2.cathode, LED3.cathode, LED4.cathode, S4.Pin_1, S4.Pin_2
  N18: U1.D4, Part2.TX_LV
  N19: U1.3V3, Part2.LV, R12.Pin_0
  N20: U1.D5, Part2.RX_LV
  N21: U1.D6, R11.Pin_1
  N22: U1.D7, R3.Pin_1
  N23: U1.D8, S4.Pin_3, S4.Pin_4, R12.Pin_1
  N24: LED1.anode, R3.Pin_0
  N25: R5.Pin_1, U2.A
  N26: U3.S, U2.VO
  N27: LED2.anode, R9.Pin_1
  N28: LED3.anode, R10.Pin_1
  N29: LED4.anode, R11.Pin_0

notes:
  Light sig
  Blue: SDA
  Yellow: SCL
  Smoke/Gas sig
  (Brown)
  Pull up resistor not required with my DHT11 breakout, but adding it for good meassure
  Arduino pinout
  Output leds:
  Green - A3 (System on)
  Red- A2 (Climate alert)
  Input buttons:
  left - 3
  middle - 4
  right - 5
  Analog signals
  Light - A0
  Smoke/gas - A1
  Digital
  DHT11 - 2
  Comms (i2c to logic level converter)
  SDA - A4
  SCL - A5
  LCD pinout
  VSS-> Ground
  VDD -> +5
  V0->pot->Ground
  RS -> 7
  RW -> Pulled to ground (write only)
  Enable -> 5
  B0-B3 -> Unused
  B4 -> 9
  B5 -> 10
  B6 -> 11
  B7 -> 12
  A -> 330 resisitor -> 6
  K -> Ground
  NodeMCU pinout
  Comms i2c via logic level converter
  SDA - D4
  SCL - D5
  Output LEDs
  Green - D6 (WiFi good)
  Yellow - D7 (Transmitting)
  Input button
  Send now button - D8

custom parts:
  NodeMCU V3.0: ESP8266 based NodeMCU
  MQ-3 breakout: Alcohol sensor is capable of detecting alcohol (ethanol) particles on itself and gives the information in digital form back to us to manipulate with it. SKU:101251 • Voltage: 5V DC • Power: max 750mW • Measurement range: 0.04-4mg/L
  DHT11 Humitidy and Temperature Sensor: DHT11 Humidity and Temperature Sensor
